# Fritzing sketch UselessMachine (saved by Fritzing 0.9.3b)
breadboards: 1

parts:
  Arduino2 = Arduino Uno (Rev3)
  Part1 = Arduino MP3 Player Shield  # not connected
  J2 = Basic Servo
  J3 = Basic Servo
  Part2 = Breakout Board for Electret Microphone
  NEOPIXEL1 = Neopixel Strip -- Black (60/m)
  Power_plug1 = Power plug

nets:
  N1: Arduino2.A0, Part2.AUD
  N2: Arduino2.D8, NEOPIXEL1.+5V
  N3: Arduino2.D9_PWM, J3.pulse
  N4: Arduino2.D10_PWM/SS, J2.pulse
  GND: Arduino2.GND, J2.gnd, J3.gnd, Part2.GND, NEOPIXEL1.GND, Power_plug1.GND
  3V3: Arduino2.3V3, Part2.VCC
  VCC: J2.vcc, J3.vcc, NEOPIXEL1.DI, Power_plug1.VCC

notes:
  HAL 9000 Useless Machine
  Servos and Leds connected to external power
  Microphone connected to 3.3V
  FIXME: Arduino output PINS in this schema are not correct.
  external power 5V 3Amp

custom parts:
  Neopixel Strip -- Black (60/m): Neopixel Strip, Black, 60 pixels per meter.
